# Fritzing sketch Fritzing (saved by Fritzing 0.9.3b)
breadboards: 3

parts:
  Part1 = Arduino Mega Pro 3.3V
  FET1 = STP16NF06 N-Channel Power MOSFET [part_number=IRFZ44n]
  FET2 = STP16NF06 N-Channel Power MOSFET [part_number=IRFZ44n]
  FET3 = STP16NF06 N-Channel Power MOSFET [part_number=IRFZ44n]
  FET4 = STP16NF06 N-Channel Power MOSFET [part_number=IRFZ44n]
  FET5 = STP16NF06 N-Channel Power MOSFET [part_number=IRFZ44n]
  FET6 = STP16NF06 N-Channel Power MOSFET [part_number=IRFZ44n]
  FET7 = STP16NF06 N-Channel Power MOSFET [part_number=IRFZ44n]
  FET8 = STP16NF06 N-Channel Power MOSFET [part_number=IRFZ44n]
  J2 = screw terminal, 4 pins
  J3 = screw terminal, 4 pins
  R1 = Resistor [tolerance=±5% resistance=2.2k package=THT]
  R2 = Resistor [tolerance=±5% resistance=2.2k package=THT]
  R3 = Resistor [tolerance=±5% resistance=2.2k package=THT]
  R4 = Resistor [tolerance=±5% resistance=2.2k package=THT]
  R5 = Resistor [tolerance=±5% resistance=2.2k package=THT]
  R6 = Resistor [tolerance=±5% resistance=2.2k package=THT]
  R7 = Resistor [tolerance=±5% resistance=2.2k package=THT]
  R8 = Resistor [tolerance=±5% resistance=2.2k package=THT]
  R10 = Resistor [tolerance=±5% resistance=2.2k package=THT]
  R11 = Resistor [tolerance=±5% resistance=2.2k package=THT]
  R12 = Resistor [tolerance=±5% resistance=2.2k package=THT]
  D1 = Rectifier Diode [part_number=FR107 package="300 mil [THT]"]
  D2 = Rectifier Diode [part_number=FR107 package="300 mil [THT]"]
  D3 = Rectifier Diode [part_number=FR107 package="300 mil [THT]"]
  D4 = Rectifier Diode [part_number=FR107 package="300 mil [THT]"]
  D5 = Rectifier Diode [part_number=FR107 package="300 mil [THT]"]
  D6 = Rectifier Diode [part_number=FR107 package="300 mil [THT]"]
  D7 = Rectifier Diode [part_number=FR107 package="300 mil [THT]"]
  D8 = Rectifier Diode [part_number=FR107 package="300 mil [THT]"]
  J4 = screw terminal, 4 pins
  J5 = screw terminal, 4 pins
  Power_plug1 = Power plug
  Pololu_A2 = Pololu A4988 [package=SO16]
  Pololu_A3 = Pololu A4988 [package=SO16]
  IC1 = SHIFT REGISTER [package=dil16]
  IC2 = SHIFT REGISTER [package=dil16]
  R13 = Resistor [tolerance=±5% resistance=1k package=THT]
  R14 = Resistor [tolerance=±5% resistance=1k package=THT]
  R15 = Resistor [tolerance=±5% resistance=1k package=THT]
  R16 = Resistor [tolerance=±5% resistance=1k package=THT]
  R17 = Resistor [tolerance=±5% resistance=1k package=THT]
  R18 = Resistor [tolerance=±5% resistance=1k package=THT]
  R19 = Resistor [tolerance=±5% resistance=1k package=THT]
  R20 = Resistor [tolerance=±5% resistance=1k package=THT]
  R21 = Resistor [tolerance=±5% resistance=1k package=THT]
  R22 = Resistor [tolerance=±5% resistance=1k package=THT]
  R23 = Resistor [tolerance=±5% resistance=1k package=THT]
  R24 = Resistor [tolerance=±5% resistance=1k package=THT]
  R25 = Resistor [tolerance=±5% resistance=1k package=THT]
  R26 = Resistor [tolerance=±5% resistance=1k package=THT]
  R27 = Resistor [tolerance=±5% resistance=1k package=THT]
  R28 = Resistor [tolerance=±5% resistance=1k package=THT]
  J10 = screw terminal, 4 pins
  J11 = screw terminal, 4 pins
  J8 = double row female pin header, 8 pins [form="♀ (female)"]
  J9 = double row female pin header, 8 pins [form="♀ (female)"]
  Matrix_keypad1 = KEYPAD 4x4
  PCB2 = RTC_DS1302_module
  Part2 = LCD1602-I2C
  DHT1 = DHT11 Humitidy and Temperature Sensor
  C1 = Electrolytic Capacitor [capacitance=0.1mF package="100 mil [THT, electrolytic]"]
  R9 = Resistor [tolerance=±5% resistance=2.2k package=THT]
  IC3 = L293D [package=THT]
  IC4 = L293D [package=THT]
  U1 = Mini-360 DC-DC Buck converter [package=THT]
  C3 = Capacitor [package=cap-pth-small]
  C4 = Capacitor [package=cap-pth-small]
  C5 = Capacitor [package=cap-pth-small]
  C6 = Capacitor [package=cap-pth-small]
  J6 = screw terminal, 2 pins  # not connected
  R29 = Resistor [tolerance=±5% resistance=1k package=THT]
  R30 = Resistor [tolerance=±5% resistance=1k package=THT]
  R31 = Resistor [tolerance=±5% resistance=1k package=THT]
  R32 = Resistor [tolerance=±5% resistance=1k package=THT]
  R33 = Resistor [tolerance=±5% resistance=1k package=THT]
  R34 = Resistor [tolerance=±5% resistance=1k package=THT]
  R35 = Resistor [tolerance=±5% resistance=220 package="1206 [SMD]"]

nets:
  N1: Part1.PE4, R9.Pin_0, IC3.Enable_1
  N2: Part1.PE5, R11.Pin_1, IC3.Enable_2
  N3: Part1.PG5, R10.Pin_0, IC4.Enable_1
  N4: Part1.PE3, R12.Pin_1, IC4.Enable_2
  VCC: Part1.VCC, PCB2.VCC, DHT1.VDD, R35.Pin_0
  N5: Part1.PH4, IC1.G, IC2.G
  N6: Part1.PH5, IC2.SER
  N7: Part1.PH6, IC1.RCK, IC2.RCK
  N8: Part1.PB4, IC1.SCK, IC2.SCK
  N9: Part1.PB5, PCB2.CLK
  N10: Part1.PB6, PCB2.DAT
  N11: Part1.PB7, PCB2.RST
  N12: Part1.SDA, Part2.SDA
  N13: Part1.SCL, Part2.SCL
  N14: Part1.PA0, FET1.gate, R1.Pin_0
  N15: Part1.PA1, FET2.gate, R2.Pin_0
  N16: Part1.PA2, FET4.gate, R3.Pin_0
  N17: Part1.PA3, FET3.gate, R4.Pin_0
  N18: Part1.PA4, FET6.gate, R5.Pin_0
  N19: Part1.PA5, FET5.gate, R6.Pin_0
  N20: Part1.PA6, FET8.gate, R7.Pin_0
  N21: Part1.PA7, FET7.gate, R8.Pin_0
  N22: Part1.PC7, Pololu_A3.DIR, R29.Pin_0
  N23: Part1.PC6, Pololu_A3.ENABLE, R31.Pin_0
  N24: Part1.PC5, Pololu_A2.DIR, R33.Pin_0
  N25: Part1.PC4, Pololu_A2.ENABLE, R32.Pin_0
  N26: Part1.PL5, Pololu_A3.STEP, R30.Pin_0
  N27: Part1.PL4, Pololu_A2.STEP, R34.Pin_0
  N28: Part1.PL3, Matrix_keypad1.row1
  N29: Part1.PL2, Matrix_keypad1.row2
  N30: Part1.PL1, Matrix_keypad1.row3
  N31: Part1.PL0, Matrix_keypad1.row4
  N32: Part1.PB3, Matrix_keypad1.col1
  N33: Part1.PB2, Matrix_keypad1.col2
  N34: Part1.PB1, Matrix_keypad1.col3
  N35: Part1.PB0, Matrix_keypad1.col4
  N36: Part1.A15, DHT1.DATA, R35.Pin_1
  GND: Part1.GND, FET1.source, FET2.source, FET3.source, FET4.source, FET5.source, FET6.source, FET7.source, FET8.source, R1.Pin_1, R2.Pin_1, R3.Pin_1, R4.Pin_1, R5.Pin_1, R6.Pin_1, R7.Pin_1, R8.Pin_1, R10.Pin_1, R11.Pin_0, R12.Pin_0, Power_plug1.GND, Pololu_A2.GND, Pololu_A3.GND, IC1.GND, IC2.GND, PCB2.GND, Part2.GND, DHT1.GND, C1.-, R9.Pin_1, IC3.In_1, IC3.0V, IC3.In_3, IC4.In_1, IC4.0V, IC4.In_3, U1.IN-, U1.OUT-, R29.Pin_1, R30.Pin_1, R33.Pin_1, R34.Pin_1
  N37: FET1.drain, J3.pin4, D1.anode
  N38: FET2.drain, J3.pin3, D2.anode
  N39: FET3.drain, J3.pin1, D4.anode
  N40: FET4.drain, J3.pin2, D3.anode
  N41: FET5.drain, J2.pin3, D5.anode
  N42: FET6.drain, J2.pin4, D8.anode
  N43: FET7.drain, J2.pin1, D7.anode
  N44: FET8.drain, J2.pin2, D6.anode
  N45: D1.cathode, D2.cathode, D3.cathode, D4.cathode, D5.cathode, D6.cathode, D7.cathode, D8.cathode, Power_plug1.VCC, Pololu_A2.VMOT, Pololu_A3.VMOT, C1.+, U1.IN+, R31.Pin_1, R32.Pin_1
  N46: J4.pin1, IC3.Out_3_(_Controlled_by_Enable_2_), C4.2
  N47: J4.pin2, IC3.Out_4_(_Controlled_by_Enable_2_), C4.1
  N48: J4.pin3, IC3.Out_2_(_Controlled_by_Enable_1_), C3.2
  N49: J4.pin4, IC3.Out_1_(_Controlled_by_Enable_1_), C3.1
  N50: J5.pin1, IC4.Out_3_(_Controlled_by_Enable_2_), C6.2
  N51: J5.pin2, IC4.Out_4_(_Controlled_by_Enable_2_), C6.1
  N52: J5.pin3, IC4.Out_2_(_Controlled_by_Enable_1_), C5.2
  N53: J5.pin4, IC4.Out_1_(_Controlled_by_Enable_1_), C5.1
  N54: Pololu_A2.RESET, Pololu_A2.SLEEP
  VCC_2: Pololu_A2.VDD, Pololu_A3.VDD, IC1.SCL, IC1.VCC, IC2.SCL, IC2.VCC, Part2.VCC, IC3.In_2, IC3.In_4, IC3.+V, IC4.In_2, IC4.+Vmotor, IC4.In_4, IC4.+V, U1.OUT+
  N55: Pololu_A2.1B, J10.pin4
  N56: Pololu_A2.1A, J10.pin3
  N57: Pololu_A2.2A, J10.pin2
  N58: Pololu_A2.2B, J10.pin1
  N59: Pololu_A3.RESET, Pololu_A3.SLEEP
  N60: Pololu_A3.1B, J11.pin4
  N61: Pololu_A3.1A, J11.pin3
  N62: Pololu_A3.2A, J11.pin2
  N63: Pololu_A3.2B, J11.pin1
  N64: IC1.QB, R24.Pin_0
  N65: IC1.QC, R23.Pin_0
  N66: IC1.QD, R27.Pin_0
  N67: IC1.QE, R22.Pin_0
  N68: IC1.QF, R26.Pin_0
  N69: IC1.QG, R25.Pin_0
  N70: IC1.QH, R28.Pin_0
  N71: IC1.SER, IC2.QH*
  N72: IC1.QA, R21.Pin_0
  N73: IC2.QB, R14.Pin_0
  N74: IC2.QC, R15.Pin_0
  N75: IC2.QD, R17.Pin_0
  N76: IC2.QE, R16.Pin_0
  N77: IC2.QF, R19.Pin_0
  N78: IC2.QG, R18.Pin_0
  N79: IC2.QH, R20.Pin_0
  N80: IC2.QA, R13.Pin_0
  N81: R13.Pin_1, J9.pin1
  N82: R14.Pin_1, J9.pin2
  N83: R15.Pin_1, J9.pin3
  N84: R16.Pin_1, J9.pin5
  N85: R17.Pin_1, J9.pin4
  N86: R18.Pin_1, J9.pin7
  N87: R19.Pin_1, J9.pin6
  N88: R20.Pin_1, J9.pin8
  N89: R21.Pin_1, J8.pin1
  N90: R22.Pin_1, J8.pin5
  N91: R23.Pin_1, J8.pin3
  N92: R24.Pin_1, J8.pin2
  N93: R25.Pin_1, J8.pin7
  N94: R26.Pin_1, J8.pin6
  N95: R27.Pin_1, J8.pin4
  N96: R28.Pin_1, J8.pin8

notes:
  V1
  V2
  V8
  M1
  M2
  M4
  12V RAIL
  MOSFET PINS:
  V1 : 22
  V2: 23
  V3: 24
  V5: 25
  V6: 26
  V7: 27
  V8: 28
  M1: 29
  M2: 30
  M3: 31
  M4: 32
  M3
  KEYPAD PIN
  R1: 46
  R2: 47
  R3: 48
  R4: 49
  C1: 50
  C2: 51
  C3: 52
  C4: 53
  STEPPERS PINS:
  STEPPER 1:
  DIR: 30
  STP: 44
  EN: 31
  STEPPER 2:
  DIR: 32
  STP: 45
  EN: 33
  STEPPER 2
  STEPPER 1
  74H595 PINS:
  DS: 8
  LTCH: 9
  CLK: 10
  OE: 7
  5V LOGIC RAIL
  LED HEADERS
  LCD I2C PINS:
  DATA: 20
  CLOCK: 21
  DHT11 PINS:
  DATA: A15
  V3
  V4
  V5
  V6
  V7
  5v RAIL
  ST1, ST2, ST3, ST4
  BUCK CONVERTER
  RTC MODULE PINS:
  CLOCK: 11
  DATA: 12
  RESET:13
  10k Ohm

custom parts:
  STP16NF06 N-Channel Power MOSFET: STP16NF06 N-channel Power MOSFET
  KEYPAD 4x4: Matrix keypad 16 buttons, 4 rows x 4 columns
  RTC_DS1302_module: Arduino module DS1302 SPI Real Time Clock
  LCD1602-I2C: A standard character display, usually with 2x16 characters. Comes in many colors with LCM1602 IIC attached.
  DHT11 Humitidy and Temperature Sensor: DHT11 Humidity and Temperature Sensor
  Mini-360 DC-DC Buck converter: Mini-360 DC-DC Buck converter. Tiny buck step down voltage converter, input voltage 4.75 to 23V output 1 to 17V adjustable. Available from ebay and the like.
